// Digital circuit add_sub.dig as structural Verilog
module add_sub (
  input  [31:0] B,
  input  [31:0] A,
  input  Sub,
  output [31:0] Sum,
  output Negative,
  output Overflow,
  output C
);

  wire and_1_out, and_2_out;
  wire [31:0] bitextender_1_out, X;

  BitExtender #(.inputBits(1), .outputBits(32)) bitextender_1 (.in(Sub), .out(bitextender_1_out));
  assign X = B ^ bitextender_1_out;  // XOr xor_1, 32 bits wide
  Add #(.Bits(32)) add_1 (.a(A), .b(X), .c_i(Sub), .s({Negative, Sum[30:0]}), .c_o(C));
  and and_1 (and_1_out, ~A[31], ~X[31], Negative);  // And
  and and_2 (and_2_out, A[31], X[31], ~Negative);  // And
  or or_1 (Overflow, and_1_out, and_2_out);

  assign Sum[31] = Negative;

  // Other names for the same wires on the sheet: A_31 = A[31]; S[31:0] = {Negative, Sum[30:0]}; S_31 = Negative;
  //   X_31 = X[31]
endmodule

/* Test case Add/Sub Test:
A B Sub Sum Negative Overflow C
# Add
0x289322c4 0x01846399 0 0x2a17865d 0 0 0
0x4152a22d 0x22042121 0 0x6356c34e 0 0 0
0x84893212 0x0994ad1a 0 0x8e1ddf2c 1 0 0
0x90a8826c 0x112109fb 0 0xa1c98c67 1 0 0
0x5210c12d 0x3d04abbc 0 0x8f156ce9 1 1 0
0x90d194b5 0xb005500e 0 0x40d6e4c3 0 1 1

# Subtract
0x39332544 0x0435fcad 1 0x34fd2897 0 0 1
0x59286ab1 0x221fb76c 1 0x3708b345 0 0 1
0xecd55935 0x248c5a4b 1 0xc848feea 1 0 1
0x902a9525 0xe5454d48 1 0xaae547dd 1 0 0
0x8211036a 0x7b13890a 1 0x06fd7a60 0 1 1
0x5fe15dbe 0x8934b9b1 1 0xd6aca40d 1 1 0
*/
