// Digital circuit comparator.dig as structural Verilog
module comparator (
  input  Negative,
  input  Overflow,
  input  C,
  input  Bool_0,
  output A_lt_B
);

  wire not_1_out, xor_1_out;

  xor xor_1 (xor_1_out, Negative, Overflow);
  not not_1 (not_1_out, C);
  Multiplexer multiplexer_1 (.sel(Bool_0), .in_0(xor_1_out), .in_1(not_1_out), .out(A_lt_B));
endmodule

/* Test case Comparator Test:
Bool_0 Negative Overflow C A<B
# A LT B
0 0 0 x 0
0 0 1 x 1
0 1 0 x 1
0 1 1 x 0

# A LTU B
1 x x 0 1
1 x x 1 0
*/
