// Digital circuit shifter.dig as structural Verilog
module shifter (
  input  [31:0] A,
  input  [31:0] B,
  input  [1:0] Bool,
  output [31:0] C
);

  wire A_gt_32;
  wire [5:0] shamt;
  wire [31:0] sll, sra, srl;

  BarrelShifter #(.Bits(32)) u_sll (.in(B), .shift(shamt), .out(sll));
  Comparator #(.Bits(32)) comparator_1 (.a(A), .b(32'h20), .gt(A_gt_32));  // open: eq, lt
  BarrelShifter #(.Bits(32), .direction("right")) u_srl (.in(B), .shift(shamt), .out(srl));
  Multiplexer #(.Selector_Bits(2), .Bits(32)) multiplexer_1 (
    .sel(Bool), .in_0(sll), .in_1(32'hdeadbeef), .in_2(srl), .in_3(sra), .out(C));
  BarrelShifter #(.Bits(32), .barrelShifterMode("arithmetic"), .direction("right")) u_sra (
    .in(B), .shift(shamt), .out(sra));
  Multiplexer #(.Bits(6)) multiplexer_2 (.sel(A_gt_32), .in_0(A[5:0]), .in_1(6'b100000), .out(shamt));

  // Other names for the same wires on the sheet: A_5_0[5:0] = A[5:0]
endmodule

/* Test case Bidirectional Shifter Test:
A B Bool C
# sll
0 0xdeadbeef 0 0xdeadbeef
8 0xdeadbeef 0 0xadbeef00
16 0xdeadbeef 0 0xbeef0000
24 0xdeadbeef 0 0xef000000
32 0xdeadbeef 0 0
33 0xdeadbeef 0 0
0xffffffff 0xdeadbeef 0 0

# srl
0 0xdeadbeef 2 0xdeadbeef
8 0xdeadbeef 2 0xdeadbe
16 0xdeadbeef 2 0xdead
24 0xdeadbeef 2 0xde
32 0xdeadbeef 2 0
33 0xdeadbeef 2 0
0xffffffff 0xdeadbeef 0 0

# sra (MSB 1)
0 0xdeadbeef 3 0xdeadbeef
8 0xdeadbeef 3 0xffdeadbe
16 0xdeadbeef 3 0xffffdead
24 0xdeadbeef 3 0xffffffde
32 0xdeadbeef 3 0xffffffff
33 0xdeadbeef 3 0xffffffff
0xffffffff 0xdeadbeef 3 0xffffffff

# sra (MSB 0)
0 0x7eadbeef 3 0x7eadbeef
8 0x7eadbeef 3 0x7eadbe
16 0x7eadbeef 3 0x7ead
24 0x7eadbeef 3 0x7e
32 0x7eadbeef 3 0
33 0x7eadbeef 3 0
0xffffffff 0x7eadbeef 3 0
*/
