// Digital circuit control_unit.dig as structural Verilog
module control_unit (
  input  [5:0] opcode,
  input  [5:0] funct,
  input  Z,
  output WERF,
  output [1:0] WDSEL,
  output [1:0] WASEL,
  output [1:0] ASEL,
  output BSEL,
  output SgnExt,
  output Wr,
  output [4:0] ALUFN,
  output [1:0] PCSEL
);

  wire and_1_out, and_2_out, and_3_out, and_4_out, and_5_out, and_6_out, and_7_out, and_8_out, B,
       comparator_1_eq, comparator_2_eq, comparator_3_eq, comparator_4_eq, comparator_5_eq, comparator_6_eq,
       comparator_7_eq, comparator_8_eq, comparator_9_eq, comparator_14_eq, comparator_15_eq,
       comparator_16_eq, comparator_17_eq, comparator_18_eq, comparator_19_eq, comparator_20_eq,
       comparator_21_eq, comparator_22_eq, comparator_23_eq, comparator_24_eq, comparator_25_eq, EQ, J, NE, R;
  wire [1:0] multiplexer_1_out, multiplexer_2_out, multiplexer_3_out, multiplexer_4_out, multiplexer_5_out;
  wire [4:0] InstructionIndex;

  Comparator #(.Bits(6)) comparator_1 (.a(funct), .b(6'b100000), .eq(comparator_1_eq));  // open: gt, lt
  Comparator #(.Bits(6)) comparator_2 (.a(funct), .b(6'b100010), .eq(comparator_2_eq));  // open: gt, lt
  Comparator #(.Bits(6)) comparator_3 (.a(funct), .b(6'b100100), .eq(comparator_3_eq));  // open: gt, lt
  Comparator #(.Bits(6)) comparator_4 (.a(funct), .b(6'b100101), .eq(comparator_4_eq));  // open: gt, lt
  Comparator #(.Bits(6)) comparator_5 (.a(funct), .b(6'b100110), .eq(comparator_5_eq));  // open: gt, lt
  Comparator #(.Bits(6)) comparator_6 (.a(funct), .b(6'b100111), .eq(comparator_6_eq));  // open: gt, lt
  Comparator #(.Bits(6)) comparator_7 (.a(funct), .b(6'b101010), .eq(comparator_7_eq));  // open: gt, lt
  Comparator #(.Bits(6)) comparator_8 (.a(funct), .b(6'b101011), .eq(comparator_8_eq));  // open: gt, lt
  Comparator #(.Bits(6)) comparator_9 (.a(opcode), .b({6{1'b0}}), .eq(comparator_9_eq));  // open: gt, lt
  Comparator #(.Bits(6)) comparator_10 (.a(opcode), .b({6{1'b0}}), .eq(R));  // open: gt, lt
  Comparator #(.Bits(6)) comparator_11 (.a(opcode), .b(6'b000010), .eq(J));  // open: gt, lt
  Comparator #(.Bits(6)) comparator_12 (.a(opcode), .b(6'b000100), .eq(EQ));  // open: gt, lt
  Comparator #(.Bits(6)) comparator_13 (.a(opcode), .b(6'b000101), .eq(NE));  // open: gt, lt
  or or_1 (B, EQ, NE);
  and and_1 (and_1_out, comparator_9_eq, comparator_1_eq);
  and and_2 (and_2_out, comparator_9_eq, comparator_2_eq);
  and and_3 (and_3_out, comparator_9_eq, comparator_3_eq);
  and and_4 (and_4_out, comparator_9_eq, comparator_4_eq);
  and and_5 (and_5_out, comparator_9_eq, comparator_5_eq);
  and and_6 (and_6_out, comparator_9_eq, comparator_6_eq);
  and and_7 (and_7_out, comparator_9_eq, comparator_7_eq);
  and and_8 (and_8_out, comparator_9_eq, comparator_8_eq);
  Comparator #(.Bits(6)) comparator_14 (.a(opcode), .b(6'b000010), .eq(comparator_14_eq));  // open: gt, lt
  Comparator #(.Bits(6)) comparator_15 (.a(opcode), .b(6'b000100), .eq(comparator_15_eq));  // open: gt, lt
  Comparator #(.Bits(6)) comparator_16 (.a(opcode), .b(6'b000101), .eq(comparator_16_eq));  // open: gt, lt
  Comparator #(.Bits(6)) comparator_17 (.a(opcode), .b(6'b001000), .eq(comparator_17_eq));  // open: gt, lt
  Comparator #(.Bits(6)) comparator_18 (.a(opcode), .b(6'b001001), .eq(comparator_18_eq));  // open: gt, lt
  Comparator #(.Bits(6)) comparator_19 (.a(opcode), .b(6'b001010), .eq(comparator_19_eq));  // open: gt, lt
  Comparator #(.Bits(6)) comparator_20 (.a(opcode), .b(6'b001011), .eq(comparator_20_eq));  // open: gt, lt
  Comparator #(.Bits(6)) comparator_21 (.a(opcode), .b(6'b001100), .eq(comparator_21_eq));  // open: gt, lt
  Comparator #(.Bits(6)) comparator_22 (.a(opcode), .b(6'b001101), .eq(comparator_22_eq));  // open: gt, lt
  Comparator #(.Bits(6)) comparator_23 (.a(opcode), .b(6'b001110), .eq(comparator_23_eq));  // open: gt, lt
  Comparator #(.Bits(6)) comparator_24 (.a(opcode), .b(6'b100011), .eq(comparator_24_eq));  // open: gt, lt
  Comparator #(.Bits(6)) comparator_25 (.a(opcode), .b(6'b101011), .eq(comparator_25_eq));  // open: gt, lt
  PriorityEncoder #(.Selector_Bits(5)) priorityencoder_1 (
    .in0(and_1_out), .in1(and_2_out), .in2(and_3_out), .in3(and_4_out), .in4(and_5_out), .in5(and_6_out),
    .in6(and_7_out), .in7(and_8_out), .in8(comparator_14_eq), .in9(comparator_15_eq),
    .in10(comparator_16_eq), .in11(comparator_17_eq), .in12(comparator_18_eq), .in13(comparator_19_eq),
    .in14(comparator_20_eq), .in15(comparator_21_eq), .in16(comparator_22_eq), .in17(comparator_23_eq),
    .in18(comparator_24_eq), .in19(comparator_25_eq), .in20(1'b0), .in21(1'b0), .in22(1'b0), .in23(1'b0),
    .in24(1'b0), .in25(1'b0), .in26(1'b0), .in27(1'b0), .in28(1'b0), .in29(1'b0), .in30(1'b0), .in31(1'b0),
    .num(InstructionIndex));  // open: any
  ROM #(.AddrBits(5), .Bits(15)) Controls (
    .A(InstructionIndex), .sel(1'b1), .D({WERF, WDSEL, WASEL, ASEL, BSEL, SgnExt, Wr, ALUFN}));
  Multiplexer #(.Bits(2)) multiplexer_1 (.sel(Z), .in_0(2'b01), .in_1(2'b00), .out(multiplexer_1_out));
  Multiplexer #(.Bits(2)) multiplexer_2 (.sel(Z), .in_0(2'b00), .in_1(2'b01), .out(multiplexer_2_out));
  Multiplexer #(.Bits(2)) multiplexer_3 (
    .sel(EQ), .in_0(multiplexer_1_out), .in_1(multiplexer_2_out), .out(multiplexer_3_out));
  Multiplexer #(.Bits(2)) multiplexer_4 (.sel(B), .in_0(2'b00), .in_1(multiplexer_3_out), .out(multiplexer_4_out));
  Multiplexer #(.Bits(2)) multiplexer_5 (.sel(J), .in_0(multiplexer_4_out), .in_1(2'b10), .out(multiplexer_5_out));
  Multiplexer #(.Bits(2)) multiplexer_6 (.sel(R), .in_0(multiplexer_5_out), .in_1(2'b00), .out(PCSEL));

  // Other names for the same wires on the sheet: opcode_0 = opcode[0]; opcode_1 = opcode[1]; opcode_2 = opcode[2];
  //   opcode_3 = opcode[3]; opcode_4 = opcode[4]; opcode_5 = opcode[5]

  // Notes on the sheet:
  //   contents of Controls (hex, n*v repeats v):
  //   5001,5011,5000,5004,5008,500c,5013,5017,0,51,51,54c1,54c1,54d3
  //   ,54d7,5480,5484,5488,64c1,e1
endmodule

/* Test case add:
opcode funct Z WERF WDSEL WASEL ASEL BSEL SgnExt Wr ALUFN PCSEL
0 32 x 1 1 0 0 0 0 0 1 0
*/
