// Digital circuit register_file.dig as structural Verilog
module register_file (
  input  [4:0] WA,
  input  WE,
  input  [31:0] WD,
  input  CLK,
  input  [4:0] RA1,
  input  [4:0] RA2,
  output [31:0] RD1,
  output [31:0] RD2
);

  wire RA1_eq__eq_0, RA2_eq__eq_0;
  wire [31:0] Da, Db;

  RegisterFile #(.AddrBits(5), .Bits(32)) registerfile_1 (
    .Din(WD), .we(WE), .Rw(WA), .C(CLK), .Ra(RA1), .Rb(RA2), .Da(Da), .Db(Db));
  nor nor_1 (RA1_eq__eq_0, RA1[0], RA1[1], RA1[2], RA1[3], RA1[4]);
  nor nor_2 (RA2_eq__eq_0, RA2[0], RA2[1], RA2[2], RA2[3], RA2[4]);
  Multiplexer #(.Bits(32)) multiplexer_1 (.sel(RA1_eq__eq_0), .in_0(Da), .in_1({32{1'b0}}), .out(RD1));
  Multiplexer #(.Bits(32)) multiplexer_2 (.sel(RA2_eq__eq_0), .in_0(Db), .in_1({32{1'b0}}), .out(RD2));
endmodule

/* Test case Register File Test:
WA WD WE CLK RA1 RA2 RD1 RD2

# $1 = 25
1 25 1 C 1 0 25 0

# $2 = 30
2 30 1 C 0 2 0 30

# $(n+1) = (n+1)
loop(n, 30)
	(n+1) (n+1) 1 C (n+1) (n) (n+1) (n)
end loop

# $(n+1) = n-60
loop(n, 30)
	(n+1) (n-60) 1 C (n+1) (n+1) (n-60) (n-60)
end loop

# Try writing to $0, which should not write anything
0 25 1 C 0 0 0 0

# Try writing when WE = 0
# The registers should still have their old values
loop(n, 30)
	(n+1) (n+80) 0 C (n+1) (n+1) (n-60) (n-60)
end loop
*/
